# Fritzing sketch chess (saved by Fritzing 0.9.3b)
breadboards: 1

parts:
  IC2 = MCP23017 I2C I/O Expander
  Part2 = HT16K33 Breakout 16x8 LED Matrix Driver [part_number=1427]
  LED_catodes = male pin header, 8 pins [form="♂ (male)"]
  led_anodes = male pin header, 8 pins [form="♂ (male)"]
  J7 = male pin header, 8 pins [form="♂ (male)"]
  J8 = male pin header, 8 pins [form="♂ (male)"]
  5V = female pin header, 1 pin [form="♀ (female)"]
  gnd = female pin header, 1 pin [form="♀ (female)"]
  GND = female pin header, 1 pin [form="♀ (female)"]
  GND_2 = female pin header, 1 pin [form="♀ (female)"]
  GND_3 = female pin header, 1 pin [form="♀ (female)"]
  5V_2 = female pin header, 1 pin [form="♀ (female)"]
  5V_3 = female pin header, 1 pin [form="♀ (female)"]
  5V_4 = female pin header, 1 pin [form="♀ (female)"]
  sda1 = female pin header, 1 pin [form="♀ (female)"]
  scl1 = female pin header, 1 pin [form="♀ (female)"]
  J49 = female pin header, 2 pins [form="♀ (female)"]  # not connected
  slc = female pin header, 1 pin [form="♀ (female)"]
  sda = female pin header, 1 pin [form="♀ (female)"]
  VCC2 = Battery  # not connected

nets:
  N1: IC2.GPB0, J7.pin8
  N2: IC2.GPB1, J7.pin7
  N3: IC2.GPB2, J7.pin6
  N4: IC2.GPB3, J7.pin5
  N5: IC2.GPB4, J7.pin4
  N6: IC2.GPB5, J7.pin3
  N7: IC2.GPB6, J7.pin2
  N8: IC2.GPB7, J7.pin1
  N9: IC2.VDD, 5V_2.pin1
  N10: IC2.VSS, GND.pin1
  N11: IC2.SCL, slc.pin1
  N12: IC2.SDA, sda.pin1
  N13: IC2.A0, 5V_4.pin1
  N14: IC2.A1, GND_3.pin1
  N15: IC2.A2, GND_2.pin1
  N16: IC2.RESET, 5V_3.pin1
  N17: IC2.GPA0, J8.pin1
  N18: IC2.GPA1, J8.pin2
  N19: IC2.GPA2, J8.pin3
  N20: IC2.GPA3, J8.pin4
  N21: IC2.GPA4, J8.pin5
  N22: IC2.GPA5, J8.pin6
  N23: IC2.GPA6, J8.pin7
  N24: IC2.GPA7, J8.pin8
  N25: Part2.A7, led_anodes.pin8
  N26: Part2.A6, led_anodes.pin7
  N27: Part2.A5, led_anodes.pin6
  N28: Part2.A4, led_anodes.pin5
  N29: Part2.A3, led_anodes.pin4
  N30: Part2.A2, led_anodes.pin3
  N31: Part2.A1, led_anodes.pin2
  N32: Part2.A0, led_anodes.pin1
  N33: Part2.SCL, scl1.pin1
  N34: Part2.SDA, sda1.pin1
  N35: Part2.VDD, 5V.pin1
  N36: Part2.GND, gnd.pin1
  N37: Part2.C0, LED_catodes.pin1
  N38: Part2.C1, LED_catodes.pin2
  N39: Part2.C2, LED_catodes.pin3
  N40: Part2.C3, LED_catodes.pin4
  N41: Part2.C4, LED_catodes.pin5
  N42: Part2.C5, LED_catodes.pin6
  N43: Part2.C6, LED_catodes.pin7
  N44: Part2.C7, LED_catodes.pin8

notes:
  cut

custom parts:
  MCP23017 I2C I/O Expander: The MCP23017 uses two i2c pins (these can be shared with other i2c devices), and in exchange gives you 16 general purpose pins. You can set each of 16 pins to be input, output, input with a pullup or open drain. There's even the ability to get an interrupt via an external pin when any of the inputs change so you don't have to keep polling the chip.
  HT16K33 Breakout 16x8 LED Matrix Driver: This is the magic sauce in our 7-segment and matrix backpacks, now available in breadboard-friendly breakout board format. The HT16K33 is a neat little chip that has the ability to drive a multiplexed 16x8 matrix (that's 128 individual LEDs). The communication protocol is I2C so it uses only 2 pins, and you can have up to 8 selectable I2C addresses so thats a total of 8 matrices, each one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
