# Fritzing sketch kk (saved by Fritzing 0.9.3b)
circuit board: 4.08923cm x 4.24369cm
breadboards: 1

parts:
  IC1 = MCP23017 I2C I/O Expander
  Part1 = HT16K33 Breakout 16x8 LED Matrix Driver [part_number=1427]
  J3 = male pin header, 3 pins [form="♂ (male)"]
  J5 = male pin header, 2 pins [form="♂ (male)"]
  J4 = male pin header, 8 pins [form="♂ (male)"]
  J2 = male pin header, 3 pins [form="♂ (male)"]
  J8 = female pin header, 2 pins [form="♀ (female)"]
  J9 = female pin header, 3 pins [form="♀ (female)"]

nets:
  N1: IC1.GPB0, J5.pin1, J5.pin2
  5V: IC1.VDD, IC1.A0, IC1.RESET, Part1.VDD, J9.pin3
  GND: IC1.VSS, IC1.A1, IC1.A2, Part1.GND, J9.pin1, J9.pin2
  N2: IC1.SCL, Part1.SCL, J8.pin2
  N3: IC1.SDA, Part1.SDA, J8.pin1
  N4: IC1.GPA0, J4.pin8
  N5: IC1.GPA1, J4.pin7
  N6: IC1.GPA2, J4.pin6
  N7: IC1.GPA3, J4.pin5
  N8: IC1.GPA4, J4.pin4
  N9: IC1.GPA5, J4.pin3
  N10: IC1.GPA6, J4.pin2
  N11: IC1.GPA7, J4.pin1
  N12: Part1.A2, J2.pin3
  N13: Part1.A1, J2.pin2
  N14: Part1.A0, J2.pin1
  N15: Part1.C1, J3.pin3
  N16: Part1.C2, J3.pin2
  N17: Part1.C3, J3.pin1

custom parts:
  MCP23017 I2C I/O Expander: The MCP23017 uses two i2c pins (these can be shared with other i2c devices), and in exchange gives you 16 general purpose pins. You can set each of 16 pins to be input, output, input with a pullup or open drain. There's even the ability to get an interrupt via an external pin when any of the inputs change so you don't have to keep polling the chip.
  HT16K33 Breakout 16x8 LED Matrix Driver: This is the magic sauce in our 7-segment and matrix backpacks, now available in breadboard-friendly breakout board format. The HT16K33 is a neat little chip that has the ability to drive a multiplexed 16x8 matrix (that's 128 individual LEDs). The communication protocol is I2C so it uses only 2 pins, and you can have up to 8 selectable I2C addresses so thats a total of 8 matrices, each one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
