# Fritzing sketch tictactoc (saved by Fritzing 0.9.3b)
circuit board: 7.23286cm x 5.07166cm
breadboards: 1

parts:
  LED1 = LED - 5mm [color="Green (570nm)" current=0.030 package="5 mm [THT]"]
  LED3 = LED - 5mm [color="Green (570nm)" current=0.030 package="5 mm [THT]"]
  LED4 = LED - 5mm [color="Green (570nm)" current=0.030 package="5 mm [THT]"]
  LED5 = LED - 5mm [color="Green (570nm)" current=0.030 package="5 mm [THT]"]
  LED6 = LED - 5mm [color="Green (570nm)" current=0.030 package="5 mm [THT]"]
  LED7 = LED - 5mm [color="Green (570nm)" current=0.030 package="5 mm [THT]"]
  LED8 = LED - 5mm [color="Green (570nm)" current=0.030 package="5 mm [THT]"]
  LED9 = LED - 5mm [color="Green (570nm)" current=0.030 package="5 mm [THT]"]
  LED2 = LED - 5mm [color="Green (570nm)" current=0.030 package="5 mm [THT]"]
  S1 = Reed switch [package=THT]
  S2 = Reed switch [package=THT]
  S3 = Reed switch [package=THT]
  S6 = Reed switch [package=THT]
  S5 = Reed switch [package=THT]
  S4 = Reed switch [package=THT]
  S9 = Reed switch [package=THT]
  S8 = Reed switch [package=THT]
  S7 = Reed switch [package=THT]
  IC1 = MCP23017 I2C I/O Expander
  Part1 = HT16K33 Breakout 16x8 LED Matrix Driver [part_number=1427]
  J1 = female pin header, 3 pins [form="♀ (female)"]
  Raspberry_Pi_1 = Raspberry Pi 3 [part_number=RPI-3-V1.2]  # not connected
  J3 = male pin header, 3 pins [form="♂ (male)"]
  J5 = male pin header, 2 pins [form="♂ (male)"]
  J4 = male pin header, 8 pins [form="♂ (male)"]
  J2 = male pin header, 3 pins [form="♂ (male)"]
  J7 = female pin header, 2 pins [form="♀ (female)"]  # not connected
  J8 = female pin header, 2 pins [form="♀ (female)"]
  J10 = female pin header, 3 pins [form="♀ (female)"]
  J6 = female pin header, 8 pins [form="♀ (female)"]  # not connected
  J11 = female pin header, 2 pins [form="♀ (female)"]  # not connected
  J9 = female pin header, 3 pins [form="♀ (female)"]

nets (from the schematic view):
  N1: LED1.cathode, LED4.cathode, LED7.cathode, J10.pin3
  a2: LED1.anode, LED3.anode, LED2.anode, J1.pin3
  N2: LED3.cathode, LED6.cathode, LED9.cathode, J10.pin1
  a1: LED4.anode, LED5.anode, LED6.anode, J1.pin2
  N3: LED5.cathode, LED8.cathode, LED2.cathode, J10.pin2
  a0: LED7.anode, LED8.anode, LED9.anode, J1.pin1
  N4: S1.pin_1, S2.pin_1, S3.pin_1, S6.pin_1, S5.pin_1, S4.pin_1, S9.pin_1, S8.pin_1, S7.pin_1
  gpa7**: S1.pin_2
  gpa6**: S2.pin_2
  gpa5**: S3.pin_2
  gpa2**: S6.pin_2
  gpa3**: S5.pin_2
  gpa4**: S4.pin_2
  gpb0**: S9.pin_2
  gpa0**: S8.pin_2
  gpa1**: S7.pin_2
  N5: IC1.GPB0, J5.pin2
  5V: IC1.VDD, IC1.A0, IC1.RESET, Part1.VDD, J9.pin3
  GND: IC1.VSS, IC1.A1, IC1.A2, Part1.GND, J9.pin1, J9.pin2
  N6: IC1.SCL, Part1.SCL, J8.pin2
  N7: IC1.SDA, Part1.SDA, J8.pin1
  N8: IC1.GPA0, J4.pin8
  N9: IC1.GPA1, J4.pin7
  N10: IC1.GPA2, J4.pin6
  N11: IC1.GPA3, J4.pin5
  N12: IC1.GPA4, J4.pin4
  N13: IC1.GPA5, J4.pin3
  N14: IC1.GPA6, J4.pin2
  N15: IC1.GPA7, J4.pin1
  N16: Part1.A2, J2.pin3
  N17: Part1.A1, J2.pin2
  N18: Part1.A0, J2.pin1
  N19: Part1.C1, J3.pin3
  N20: Part1.C2, J3.pin2
  N21: Part1.C3, J3.pin1

custom parts:
  MCP23017 I2C I/O Expander: The MCP23017 uses two i2c pins (these can be shared with other i2c devices), and in exchange gives you 16 general purpose pins. You can set each of 16 pins to be input, output, input with a pullup or open drain. There's even the ability to get an interrupt via an external pin when any of the inputs change so you don't have to keep polling the chip.
  HT16K33 Breakout 16x8 LED Matrix Driver: This is the magic sauce in our 7-segment and matrix backpacks, now available in breadboard-friendly breakout board format. The HT16K33 is a neat little chip that has the ability to drive a multiplexed 16x8 matrix (that's 128 individual LEDs). The communication protocol is I2C so it uses only 2 pins, and you can have up to 8 selectable I2C addresses so thats a total of 8 matrices, each one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
